# Fritzing sketch transmitter (saved by Fritzing 0.8.3b)
breadboards: 1

parts:
  Part1 = Arduino Uno (Rev3)
  U1 = RF-LINK_TX [package=rf-link_tx]  # not connected
  Part2 = SRF05 Ultrasonic Rangefinder
  Part3 = SRF05 Ultrasonic Rangefinder

nets:
  N1: Part1.D8, Part3.Trig
  N2: Part1.D9_PWM, Part2.Echo
  N3: Part1.D10_PWM/SS, Part2.Trig
  N4: Part1.D7, Part3.Echo
